# Fritzing sketch Circuit diagram (saved by Fritzing 0.9.3b)
breadboards: 1

parts:
  Part1 = Arduino Mega 2560 (Rev3)
  Part2 = Arduino Uno (Rev3) - ICSP
  HC-SR04_Sensor_1 = HC-SR04 Ultrasonic Distance Sensor
  LCD1 = LCD screen
  Matrix_keypad1 = KEYPAD 4x4
  R2 = Trimmer Potentiometer [maximum_resistance=10kΩ package=THT]
  J1 = Piezo Speaker
  R3 = Resistor [tolerance=±5% resistance=220 package=THT]

nets:
  N1: Part1.A8, Matrix_keypad1.col1
  N2: Part1.A9, Matrix_keypad1.col2
  N3: Part1.A10, Matrix_keypad1.col3
  N4: Part1.A11, Matrix_keypad1.col4
  N5: Part1.A12, Matrix_keypad1.row1
  N6: Part1.A13, Matrix_keypad1.row2
  N7: Part1.A14, Matrix_keypad1.row3
  N8: Part1.A15, Matrix_keypad1.row4
  N9: Part1.A0, HC-SR04_Sensor_1.ECHO
  N10: Part1.A1, HC-SR04_Sensor_1.TRIG
  N11: Part1.D9_PWM, Part2.D9_PWM
  N12: Part1.D8_PWM, Part2.D8
  5V: Part1.5V, Part2.5V, HC-SR04_Sensor_1.VCC, LCD1.VDD, R2.leg2, R3.Pin_0
  GND: Part1.GND, Part2.GND, HC-SR04_Sensor_1.GND, LCD1.VSS, LCD1.LED-, R2.leg1, J1.pin1
  N13: Part2.D11_PWM/MOSI, LCD1.E
  N14: Part2.D12/MISO, LCD1.RS
  N15: Part2.D2, J1.pin2
  N16: Part2.D3_PWM, LCD1.DB7
  N17: Part2.D4, LCD1.DB6
  N18: Part2.D5_PWM, LCD1.DB5
  N19: Part2.D6_PWM, LCD1.DB4
  N20: LCD1.V0, R2.wiper
  N21: LCD1.LED+, R3.Pin_1

custom parts:
  KEYPAD 4x4: Matrix keypad 16 buttons, 4 rows x 4 columns
